# Fritzing sketch lightsensor (saved by Fritzing 0.9.3b)
breadboards: 1

parts:
  R1 = Photocell (LDR) [package=THT]
  R2 = Resistor [tolerance=±5% resistance=1k package=THT]
  Part2 = Arduino Uno (Rev3)  # not connected

nets:
  N1: R1.pin_0, R2.Pin_1
