# Fritzing sketch nightlight (saved by Fritzing 0.9.3b)
breadboards: 1

parts:
  R1 = Photocell (LDR) [package=THT]
  R2 = Resistor [tolerance=±5% resistance=1k package=THT]
  LED1 = LED - 5mm [color="Red (633nm)" package="5 mm [THT]"]
  R3 = Resistor [tolerance=±5% resistance=220 package=THT]
  Part2 = Arduino Uno (Rev3)  # not connected

nets:
  N1: R1.pin_0, R2.Pin_1
  N2: R2.Pin_0, R3.Pin_1
  N3: LED1.cathode, R3.Pin_0
